# Fritzing sketch dht11_arduino_uno (saved by Fritzing 0.9.4)
breadboards: 1

parts:
  パーツ1 = Arduino Uno (Rev3)
  DHT1 = Humidity and Temperature Sensor DHT11
  R1 = Resistor [tolerance=±5% resistance=5.1k package=THT]

nets:
  N1: パーツ1.D2, DHT1.Data-signal, R1.Pin_1
  5V: パーツ1.5V, DHT1.Vcc
  N2: パーツ1.GND, DHT1.GND_2

custom parts:
  Humidity and Temperature Sensor DHT11: Digital relative humidity & temperature sensor DHT11
