# Fritzing sketch dht11_raspi (saved by Fritzing 0.9.4)
breadboards: 1

parts:
  DHT1 = Humidity and Temperature Sensor DHT11
  R1 = Resistor [tolerance=±5% resistance=5.1k package=THT]
  C1 = Ceramic Capacitor [capacitance=100nF package="100 mil [THT, multilayer]"]
  Raspberry_Pi_1 = Raspberry Pi 3 [part_number=RPI-3-V1.2]

nets:
  N1: DHT1.Data-signal, R1.Pin_1, Raspberry_Pi_1.GPIO21, Raspberry_Pi_1.GPIO20
  N2: DHT1.GND_2, C1.1, Raspberry_Pi_1.GND
  N3: R1.Pin_0, C1.0

custom parts:
  Humidity and Temperature Sensor DHT11: Digital relative humidity & temperature sensor DHT11
